// Logisim project ALU_IC.circ as structural Verilog: 1 circuit, main circuit main
module main (
  input  CS0,
  input  CS1,
  input  CS2,
  input  A1,
  input  B1,
  input  A2,
  input  B2,
  input  A3,
  input  B3,
  input  A4,
  input  B4,
  output F1,
  output F2,
  output F3,
  output F4,
  output C,
  output V,
  output Z,
  output S
);

  wire dip_7404_1_p7, dip_7408_1_p1, dip_7408_1_p3, dip_7408_1_p6, dip_7408_1_p7, dip_7408_1_p9,
       dip_7408_1_p10, dip_7408_1_p12, dip_7408_2_p1, dip_7408_2_p3, dip_7408_2_p6, dip_7408_2_p9,
       dip_7408_2_p11, dip_7408_2_p12, dip_7408_3_p3, dip_7408_3_p6, dip_7408_3_p8, dip_7408_4_p3,
       dip_7408_4_p6, dip_7408_4_p8, dip_7432_1_p3, dip_7432_1_p6, dip_7432_1_p8, dip_7432_2_p3,
       dip_7432_2_p6, dip_7432_2_p9, dip_7486_1_p3, dip_7486_1_p4;

  // DIP_7486 dip_7486_1: pin names not known; wires that end beside it: CS1, CS2, dip_7486_1_p3, dip_7486_1_p4, C, V
  // DIP_7408 dip_7408_1: pin names not known; wires that end beside it: dip_7408_1_p1, CS2, dip_7408_1_p3, dip_7408_1_p3, B1, dip_7408_1_p6, dip_7408_1_p7, CS0, dip_7408_1_p9, dip_7408_1_p10, B1, dip_7408_1_p12
  // DIP_7408 dip_7408_2: pin names not known; wires that end beside it: dip_7408_2_p1, dip_7408_1_p7, dip_7408_2_p3, B2, dip_7408_1_p3, dip_7408_2_p6, B2, dip_7408_1_p10, dip_7408_2_p9, dip_7408_1_p7, dip_7408_2_p11, dip_7408_2_p12
  // DIP_7408 dip_7408_3: pin names not known; wires that end beside it: B3, dip_7408_1_p3, dip_7408_3_p3, B3, dip_7408_1_p10, dip_7408_3_p6, dip_7408_1_p7, dip_7408_3_p8, dip_7486_1_p4
  // DIP_7408 dip_7408_4: pin names not known; wires that end beside it: B4, dip_7408_1_p3, dip_7408_4_p3, B4, dip_7408_1_p10, dip_7408_4_p6, dip_7408_1_p7, dip_7408_4_p8, C
  // DIP_7404 dip_7404_1: pin names not known; wires that end beside it: CS1, dip_7408_1_p1, dip_7486_1_p3, dip_7408_1_p10, CS2, dip_7408_1_p7, dip_7404_1_p7, Z
  // DIP_7432 dip_7432_1: pin names not known; wires that end beside it: F1, F2, dip_7432_1_p3, A1, dip_7408_1_p6, dip_7432_1_p6, dip_7432_1_p3, dip_7432_1_p8, dip_7404_1_p7, F4, F3, dip_7432_1_p8
  // DIP_7432 dip_7432_2: pin names not known; wires that end beside it: A2, dip_7408_2_p6, dip_7432_2_p3, A3, dip_7408_3_p3, dip_7432_2_p6, dip_7408_4_p3, A4, dip_7432_2_p9
  Adder #(.width(1)) adder_1 (
    .a(dip_7432_1_p6), .b(dip_7408_1_p12), .out(F1), .cin(dip_7408_1_p9), .cout(dip_7408_2_p1));
  Adder #(.width(1)) adder_2 (
    .a(dip_7432_2_p3), .b(dip_7408_2_p9), .out(F2), .cin(dip_7408_2_p3), .cout(dip_7408_2_p11));
  Adder #(.width(1)) adder_3 (
    .a(dip_7432_2_p6), .b(dip_7408_3_p6), .out(F3), .cin(dip_7408_2_p12), .cout(dip_7408_3_p8));
  Adder #(.width(1)) adder_4 (
    .a(dip_7432_2_p9), .b(dip_7408_4_p6), .out(F4), .cin(dip_7486_1_p4), .cout(dip_7408_4_p8));

  assign S = F4;
endmodule
