// Logisim project v1.circ as structural Verilog
module module_1 (
  input  in_1,
  input  [3:0] Exponent_A,
  input  [3:0] Exponent_B,
  input  [11:0] in_4,
  input  [11:0] in_5,
  input  [10:0] Fraction_A,
  input  [10:0] Fraction_B,
  input  in_8,
  input  in_9,
  input  [3:0] Exponent_A_2,
  input  [3:0] Exponent_B_2,
  input  [10:0] Fraction_A_2,
  input  [10:0] Fraction_B_2,
  input  in_14,
  input  Sign_Bit_A,
  input  Sign_Bit_B,
  input  in_17,
  input  in_18,
  input  in_19,
  input  [3:0] Exponent_A_3,
  input  [3:0] Exponent_B_3,
  input  [10:0] Fraction_A_3,
  input  [10:0] Fraction_B_3,
  input  in_24,
  input  in_25,
  input  in_26,
  output [3:0] Exponent_Difference,
  output [10:0] Right_Shifted_Value,
  output [10:0] out_29,
  output [10:0] out_30,
  output [11:0] out_31,
  output out_32,
  output [3:0] Exponent_Difference_2,
  output [11:0] Right_Shifted_Value_2,
  output [11:0] Before_Right_Shift,
  output [11:0] Unchanged_fraction,
  output [3:0] out_37,
  output [11:0] Sum,
  output [11:0] out_39,
  output Carry,
  output [11:0] out_41,
  output [11:0] Sum_2,
  output Carry_2
);

  wire comparator_1_gt, comparator_1_lt, comparator_2_gt, comparator_2_lt, comparator_3_eq, comparator_3_gt,
       comparator_3_lt, comparator_4_eq, comparator_4_gt, comparator_4_lt, or_1_out, or_2_out;
  wire [3:0] multiplexer_5_out, multiplexer_6_out, multiplexer_7_out, multiplexer_8_out;
  wire [11:0] and_1_out, and_2_out, and_3_out, and_4_out, multiplexer_9_out, multiplexer_10_out,
       multiplexer_11_out, multiplexer_12_out;
  wire [11:11] not_1_out, xor_1_out;

  Comparator #(.width(4), .mode("unsigned")) comparator_1 (
    .a(Exponent_A), .b(Exponent_B), .gt(comparator_1_gt), .lt(comparator_1_lt));  // open: eq
  Comparator #(.width(4), .mode("unsigned")) comparator_2 (
    .a(Exponent_A_2), .b(Exponent_B_2), .gt(comparator_2_gt), .lt(comparator_2_lt));  // open: eq
  Multiplexer #(.width(11), .enable("false")) multiplexer_1 (
    .in0(Fraction_A), .in1(Fraction_B), .out(out_29), .sel(comparator_1_gt));
  Multiplexer #(.width(11), .enable("false")) multiplexer_2 (
    .in0(Fraction_A), .in1(Fraction_B), .out(out_30), .sel(comparator_1_lt));
  Multiplexer #(.width(11), .enable("false")) multiplexer_3 (
    .in0(Fraction_A_2), .in1(Fraction_B_2), .out(Before_Right_Shift[10:0]), .sel(comparator_2_gt));
  Multiplexer #(.width(11), .enable("false")) multiplexer_4 (
    .in0(Fraction_A_2), .in1(Fraction_B_2), .out(Unchanged_fraction[10:0]), .sel(comparator_2_lt));
  Multiplexer #(.width(4), .enable("false")) multiplexer_5 (
    .in0(Exponent_A), .in1(Exponent_B), .out(multiplexer_5_out), .sel(comparator_1_lt));
  Multiplexer #(.width(4), .enable("false")) multiplexer_6 (
    .in0(Exponent_A), .in1(Exponent_B), .out(multiplexer_6_out), .sel(comparator_1_gt));
  Multiplexer #(.width(4), .enable("false")) multiplexer_7 (
    .in0(Exponent_A_2), .in1(Exponent_B_2), .out(multiplexer_7_out), .sel(comparator_2_lt));
  Multiplexer #(.width(4), .enable("false")) multiplexer_8 (
    .in0(Exponent_A_2), .in1(Exponent_B_2), .out(multiplexer_8_out), .sel(comparator_2_gt));
  Subtractor #(.width(4)) subtractor_1 (
    .a(multiplexer_5_out), .b(multiplexer_6_out), .out(Exponent_Difference), .bin(in_1));  // open: bout
  Subtractor #(.width(4)) subtractor_2 (
    .a(multiplexer_7_out), .b(multiplexer_8_out), .out(Exponent_Difference_2), .bin(in_9));  // open: bout
  Shifter #(.width(11), .shift("lr")) shifter_1 (.in(out_29), .\dist (Exponent_Difference), .out(Right_Shifted_Value));
  Shifter #(.width(12), .shift("lr")) shifter_2 (
    .in({in_14, Before_Right_Shift[10:0]}), .\dist (Exponent_Difference_2), .out(Right_Shifted_Value_2));
  Comparator #(.width(12), .mode("unsigned")) comparator_3 (
    .a(in_4), .b(in_5), .gt(comparator_3_gt), .eq(comparator_3_eq), .lt(comparator_3_lt));
  Multiplexer #(.width(12), .enable("false")) multiplexer_9 (
    .in0(in_4), .in1(in_5), .out(multiplexer_9_out), .sel(or_1_out));
  or or_1 (or_1_out, comparator_3_eq, comparator_3_lt);
  Multiplexer #(.width(12), .enable("false")) multiplexer_10 (
    .in0(in_4), .in1(in_5), .out(multiplexer_10_out), .sel(comparator_3_gt));
  // Exponent exponent_1: pin names not known; wires that end beside it: Exponent_A_3, Exponent_B_3, Fraction_A_3, Fraction_B_3, in_24, in_25, in_19, out_37, out_39, out_41
  Subtractor #(.width(12)) subtractor_3 (
    .a(multiplexer_9_out), .b(multiplexer_10_out), .out(out_31), .bin(in_8), .bout(out_32));
  not not_1 (not_1_out[11], xor_1_out[11]);
  xor xor_1 (xor_1_out[11], Sign_Bit_A, Sign_Bit_B);
  assign and_1_out = {12{not_1_out[11]}} & out_39;  // AND_Gate and_1, 12 bits wide
  assign and_2_out = {12{not_1_out[11]}} & out_41;  // AND_Gate and_2, 12 bits wide
  assign and_3_out = {12{xor_1_out[11]}} & out_39;  // AND_Gate and_3, 12 bits wide
  assign and_4_out = {12{xor_1_out[11]}} & out_41;  // AND_Gate and_4, 12 bits wide
  // AND_Gate and_5 is placed but not wired
  Comparator #(.width(12), .mode("unsigned")) comparator_4 (
    .a(and_3_out), .b(and_4_out), .gt(comparator_4_gt), .eq(comparator_4_eq), .lt(comparator_4_lt));
  Multiplexer #(.width(12), .enable("false")) multiplexer_11 (
    .in0(and_3_out), .in1(and_4_out), .out(multiplexer_11_out), .sel(or_2_out));
  or or_2 (or_2_out, comparator_4_eq, comparator_4_lt);
  Multiplexer #(.width(12), .enable("false")) multiplexer_12 (
    .in0(and_3_out), .in1(and_4_out), .out(multiplexer_12_out), .sel(comparator_4_gt));
  Adder_part #(.width(12)) adder_1 (.a(and_1_out), .b(and_2_out), .out(Sum), .cin(in_18), .cout(Carry));
  Subtractor #(.width(12)) subtractor_4 (
    .a(multiplexer_11_out), .b(multiplexer_12_out), .out(Sum_2), .bin(in_26), .bout(Carry_2));

  assign Before_Right_Shift[11] = in_14;
  assign Unchanged_fraction[11] = in_17;
endmodule

// EXP
module Exponent (
  input  in_1,
  input  [3:0] Exponent_A,
  input  [3:0] Exponent_B,
  input  [10:0] Fraction_A,
  input  [10:0] Fraction_B,
  output [3:0] Larger_Exponent,
  output [3:0] Exponent_Difference,
  output [11:0] Right_Shifted_Value,
  output [11:0] Unchanged_fraction
);

  wire comparator_1_gt, comparator_1_lt;
  wire [3:0] multiplexer_4_out;
  wire [10:0] multiplexer_1_out;

  Comparator #(.width(4), .mode("unsigned")) comparator_1 (
    .a(Exponent_A), .b(Exponent_B), .gt(comparator_1_gt), .lt(comparator_1_lt));  // open: eq
  Multiplexer #(.width(11), .enable("false")) multiplexer_1 (
    .in0(Fraction_A), .in1(Fraction_B), .out(multiplexer_1_out), .sel(comparator_1_gt));
  Multiplexer #(.width(11), .enable("false")) multiplexer_2 (
    .in0(Fraction_A), .in1(Fraction_B), .out(Unchanged_fraction[10:0]), .sel(comparator_1_lt));
  Multiplexer #(.width(4), .enable("false")) multiplexer_3 (
    .in0(Exponent_A), .in1(Exponent_B), .out(Larger_Exponent), .sel(comparator_1_lt));
  Multiplexer #(.width(4), .enable("false")) multiplexer_4 (
    .in0(Exponent_A), .in1(Exponent_B), .out(multiplexer_4_out), .sel(comparator_1_gt));
  Subtractor #(.width(4)) subtractor_1 (
    .a(Larger_Exponent), .b(multiplexer_4_out), .out(Exponent_Difference), .bin(in_1));  // open: bout
  Shifter #(.width(12), .shift("lr")) shifter_1 (
    .in({1'b1, multiplexer_1_out}), .\dist (Exponent_Difference), .out(Right_Shifted_Value));

  assign Unchanged_fraction[11] = 1'b1;
endmodule

// ADDER
module Adder (
  input  Sign_Bit_A,
  input  Sign_Bit_B,
  input  in_3,
  input  in_4,
  input  [3:0] Exponent_A,
  input  [3:0] Exponent_B,
  input  [10:0] Fraction_A,
  input  [10:0] Fraction_B,
  input  in_9,
  output [3:0] Larger_Exponent,
  output [11:0] Sum,
  output Carry,
  output [11:0] Sum_2,
  output Carry_2
);

  wire comparator_1_eq, comparator_1_gt, comparator_1_lt, or_1_out;
  wire [11:0] and_1_out, and_2_out, and_3_out, and_4_out, exponent_1_right_shifted_value,
       exponent_1_unchanged_fraction, multiplexer_1_out, multiplexer_2_out;
  wire [11:11] not_1_out, xor_1_out;

  Exponent exponent_1 (
    .Exponent_A(Exponent_A), .Exponent_B(Exponent_B), .Fraction_A(Fraction_A), .Fraction_B(Fraction_B),
    .in_1(in_4), .Larger_Exponent(Larger_Exponent), .Right_Shifted_Value(exponent_1_right_shifted_value),
    .Unchanged_fraction(exponent_1_unchanged_fraction));  // open: Exponent_Difference
  not not_1 (not_1_out[11], xor_1_out[11]);
  xor xor_1 (xor_1_out[11], Sign_Bit_A, Sign_Bit_B);
  assign and_1_out = {12{not_1_out[11]}} & exponent_1_right_shifted_value;  // AND_Gate and_1, 12 bits wide
  assign and_2_out = {12{not_1_out[11]}} & exponent_1_unchanged_fraction;  // AND_Gate and_2, 12 bits wide
  assign and_3_out = {12{xor_1_out[11]}} & exponent_1_right_shifted_value;  // AND_Gate and_3, 12 bits wide
  assign and_4_out = {12{xor_1_out[11]}} & exponent_1_unchanged_fraction;  // AND_Gate and_4, 12 bits wide
  // AND_Gate and_5 is placed but not wired
  Comparator #(.width(12), .mode("unsigned")) comparator_1 (
    .a(and_3_out), .b(and_4_out), .gt(comparator_1_gt), .eq(comparator_1_eq), .lt(comparator_1_lt));
  Multiplexer #(.width(12), .enable("false")) multiplexer_1 (
    .in0(and_3_out), .in1(and_4_out), .out(multiplexer_1_out), .sel(or_1_out));
  or or_1 (or_1_out, comparator_1_eq, comparator_1_lt);
  Multiplexer #(.width(12), .enable("false")) multiplexer_2 (
    .in0(and_3_out), .in1(and_4_out), .out(multiplexer_2_out), .sel(comparator_1_gt));
  Adder_part #(.width(12)) adder_1 (.a(and_1_out), .b(and_2_out), .out(Sum), .cin(in_3), .cout(Carry));
  Subtractor #(.width(12)) subtractor_1 (
    .a(multiplexer_1_out), .b(multiplexer_2_out), .out(Sum_2), .bin(in_9), .bout(Carry_2));
endmodule
